# Fritzing sketch Circuit_Diagram (saved by Fritzing 0.9.10b)
breadboards: 1

parts:
  PMS5003 = PMS5003
  DHT11 = Humidity and Temperature Sensor DHT11
  GPS_NEO6MV2 = u-blox NEO-6M GPS Breakout
  ESP32_TTGO_V1_3 = TTGO T7-ESP32
  DISPLAY_OLED = OLED 128x64 I2C Monochrome Display GND-VDD
  MICRO_SD = Micro SD card reader
  U1 = LIPO-110mAh [package=lipo-110]
  R2 = Resistor [tolerance=±5% resistance=2.2k package="0402 [SMD]"]
  R1 = Resistor [tolerance=±5% resistance=1k package="0402 [SMD]"]
  BUTTON_2 = Pushbutton [package="[SMD]"]
  BUTTON_1 = Pushbutton [package="[SMD]"]
  RELOJ_RTC = ZS-042 RTC Module

nets (from the pcb view):
  VCC: PMS5003.Pin_1, DHT11.Vcc, GPS_NEO6MV2.Pin_1, ESP32_TTGO_V1_3.5V, MICRO_SD.Pin_1, BUTTON_1.Pin_3, BUTTON_1.Pin_4
  GND: PMS5003.Pin_2, DHT11.GND, GPS_NEO6MV2.Pin_2, ESP32_TTGO_V1_3.GND, DISPLAY_OLED.GND, MICRO_SD.Pin_6, U1.-, R1.Pin_0, RELOJ_RTC.GND
  N1: PMS5003.Pin_4, ESP32_TTGO_V1_3.32
  N2: PMS5003.Pin_5, ESP32_TTGO_V1_3.25
  N3: DHT11.Data, ESP32_TTGO_V1_3.27
  N4: GPS_NEO6MV2.Pin_3, ESP32_TTGO_V1_3.16
  N5: GPS_NEO6MV2.Pin_4, ESP32_TTGO_V1_3.17
  N6: ESP32_TTGO_V1_3.VN, U1.+
  N7: ESP32_TTGO_V1_3.18, MICRO_SD.Pin_4
  N8: ESP32_TTGO_V1_3.33, R1.Pin_1, BUTTON_1.Pin_1, BUTTON_1.Pin_2
  N9: ESP32_TTGO_V1_3.19, MICRO_SD.Pin_5
  N10: ESP32_TTGO_V1_3.34, R2.Pin_0, BUTTON_2.Pin_1, BUTTON_2.Pin_2
  N11: ESP32_TTGO_V1_3.23, MICRO_SD.Pin_3
  N12: ESP32_TTGO_V1_3.5, MICRO_SD.Pin_2
  3V3: ESP32_TTGO_V1_3.3V3, DISPLAY_OLED.VDD, BUTTON_2.Pin_4, RELOJ_RTC.VCC
  N13: ESP32_TTGO_V1_3.21, DISPLAY_OLED.SDA, RELOJ_RTC.SDA
  N14: ESP32_TTGO_V1_3.22, DISPLAY_OLED.SCK, RELOJ_RTC.SCL

custom parts:
  PMS5003: PMS5003 is a kind of digital and universal particle concentration sensor, which can be used to obtain the number of suspended particles in the air.
  Humidity and Temperature Sensor DHT11: Digital relative humidity & temperature sensor DHT11
  TTGO T7-ESP32: TTGO T7-ESP32 cpu module
  OLED 128x64 I2C Monochrome Display GND-VDD: OLED 128x64 I2C Monochrome Display. Note: there are two variants of this part, this one is the GND VDD SCK SDA variant. The other is VDD GND SCK SDA. Make sure you select the part that matches your module as using the incorrect part will probably destroy your module! In addition the mounting holes are marked on silkscreen but not by default drilled. If you want drilled mounting holes, copy a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
  Micro SD card reader: Micro SD card reader.
